// Logisim project Circuitos.circ as structural Verilog
module sr (
);

  wire and_1_out, and_2_out, and_3_out, and_4_out, and_5_out, and_6_out, and_7_out, and_8_out, and_9_out,
       and_10_out, and_11_out, and_12_out, and_13_out, and_14_out, and_15_out, and_16_out, and_17_out, b0,
       b1, b2, b3, r0, r1, r2, r3, reloj, reset, s0, s1, s2, s3;

  Clock clock_1 (.out(reloj));
  Button button_1 (.out(reset));
  and and_1 (and_1_out, ~b2, ~b3, b1);  // AND_Gate
  and and_2 (and_2_out, ~b0, b1, b2);  // AND_Gate
  and and_3 (and_3_out, ~b0, ~b1, b2);  // AND_Gate
  and and_4 (and_4_out, b1, ~b2, b3);  // AND_Gate
  and and_5 (and_5_out, b0, b1, b2);
  or or_1 (s0, and_1_out, and_2_out);
  or or_2 (r0, and_3_out, and_4_out, and_5_out);
  S_R_Flip_Flop s_r_ff_1 (.S(s3), .clk(reloj), .R(r3), .Q(b0), .preset(reset));  // open: Qn, reset, en
  S_R_Flip_Flop s_r_ff_2 (.S(s2), .clk(reloj), .R(r2), .Q(b1), .preset(reset));  // open: Qn, reset, en
  and and_6 (and_6_out, ~b0, ~b1, ~b2);  // AND_Gate
  or or_3 (s1, and_6_out, and_7_out);
  and and_7 (and_7_out, b0, b1, ~b2, ~b3);  // AND_Gate
  and and_8 (and_8_out, b1, b3);
  or or_4 (r1, and_8_out, and_9_out);
  and and_9 (and_9_out, b2, ~b3, ~b1);  // AND_Gate
  S_R_Flip_Flop s_r_ff_3 (.S(s1), .clk(reloj), .R(r1), .Q(b2), .preset(reset));  // open: Qn, reset, en
  and and_10 (and_10_out, ~b0, ~b1, b2);  // AND_Gate
  or or_5 (s2, and_10_out, and_11_out);
  and and_11 (and_11_out, ~b1, b0, b3);  // AND_Gate
  and and_12 (and_12_out, ~b2, ~b3);  // AND_Gate
  or or_6 (r2, and_12_out, and_13_out);
  and and_13 (and_13_out, b2, b3, b1);
  S_R_Flip_Flop s_r_ff_4 (.S(s0), .clk(reloj), .R(r0), .Q(b3), .preset(reset));  // open: Qn, reset, en
  and and_14 (and_14_out, ~b0, b1, ~b2);  // AND_Gate
  or or_7 (s3, and_14_out, and_15_out);
  and and_15 (and_15_out, ~b2, b3, ~b0);  // AND_Gate
  and and_16 (and_16_out, b0, ~b2);  // AND_Gate
  or or_8 (r3, and_16_out, and_17_out);
  and and_17 (and_17_out, b1, b2);
endmodule

module T (
);

  wire and_1_out, and_2_out, and_3_out, and_4_out, and_5_out, and_6_out, and_7_out, and_8_out, and_9_out,
       and_10_out, and_11_out, and_12_out, and_13_out, and_14_out, b0, b1, b2, b3, reloj, reset, t0, t1, t2,
       t3;

  Clock clock_1 (.out(reloj));
  Button button_1 (.out(reset));
  and and_1 (and_1_out, ~b2, b3);  // AND_Gate
  and and_2 (and_2_out, b1, b0);
  and and_3 (and_3_out, b1, ~b2);  // AND_Gate
  or or_1 (t3, and_1_out, and_2_out, and_3_out);
  T_Flip_Flop t_ff_1 (.clk(reloj), .T(t3), .Q(b0), .preset(reset));  // open: Qn, reset, en
  and and_4 (and_4_out, ~b0, ~b1, b2);  // AND_Gate
  and and_5 (and_5_out, b2, b3);
  and and_6 (and_6_out, ~b2, ~b3, b1);  // AND_Gate
  T_Flip_Flop t_ff_2 (.clk(reloj), .T(t2), .Q(b1), .preset(reset));  // open: Qn, reset, en
  or or_2 (t2, and_4_out, and_5_out, and_6_out, b0);
  T_Flip_Flop t_ff_3 (.clk(reloj), .T(t1), .Q(b2), .preset(reset));  // open: Qn, reset, en
  and and_7 (and_7_out, ~b0, ~b1, ~b3);  // AND_Gate
  and and_8 (and_8_out, ~b0, ~b1, ~b2);  // AND_Gate
  and and_9 (and_9_out, b2, b3, b1);
  and and_10 (and_10_out, b0, b1);
  or or_3 (t1, and_7_out, and_8_out, and_9_out, and_10_out);
  T_Flip_Flop t_ff_4 (.clk(reloj), .T(t0), .Q(b3), .preset(reset));  // open: Qn, reset, en
  and and_11 (and_11_out, ~b0, ~b1, b2, b3);  // AND_Gate
  and and_12 (and_12_out, b1, b0);
  and and_13 (and_13_out, b1, ~b3);  // AND_Gate
  and and_14 (and_14_out, b1, ~b2);  // AND_Gate
  or or_4 (t0, and_11_out, and_12_out, and_13_out, and_14_out);
endmodule

module d (
);

  wire and_1_out, and_2_out, and_3_out, and_4_out, and_5_out, and_6_out, and_7_out, and_8_out, and_9_out,
       and_10_out, and_11_out, and_12_out, and_13_out, and_14_out, and_15_out, b0, b1, b2, b3, d0, d1, d2,
       d3, reloj, reset;

  Clock clock_1 (.out(reloj));
  Button button_1 (.out(reset));
  and and_1 (and_1_out, ~b0, ~b2, b1);  // AND_Gate
  and and_2 (and_2_out, ~b0, ~b2, b3);  // AND_Gate
  and and_3 (and_3_out, b0, b2, ~b1);  // AND_Gate
  or or_1 (d3, and_1_out, and_2_out, and_3_out);
  D_Flip_Flop d_ff_1 (.clk(reloj), .D(d3), .Q(b0), .preset(reset));  // open: Qn, en, reset
  and and_4 (and_4_out, ~b0, ~b1, b2);  // AND_Gate
  and and_5 (and_5_out, b0, ~b1);  // AND_Gate
  and and_6 (and_6_out, ~b2, b3, b1);  // AND_Gate
  and and_7 (and_7_out, b2, ~b3);  // AND_Gate
  D_Flip_Flop d_ff_2 (.clk(reloj), .D(d2), .Q(b1), .preset(reset));  // open: Qn, en, reset
  or or_2 (d2, and_4_out, and_5_out, and_6_out, and_7_out);
  D_Flip_Flop d_ff_3 (.clk(reloj), .D(d1), .Q(b2), .preset(reset));  // open: Qn, en, reset
  and and_8 (and_8_out, ~b0, ~b2, ~b1);  // AND_Gate
  and and_9 (and_9_out, ~b1, b2, b3);  // AND_Gate
  and and_10 (and_10_out, b0, ~b3);  // AND_Gate
  and and_11 (and_11_out, ~b3, b2, b1);  // AND_Gate
  or or_3 (d1, and_8_out, and_9_out, and_10_out, and_11_out);
  D_Flip_Flop d_ff_4 (.clk(reloj), .D(d0), .Q(b3), .preset(reset));  // open: Qn, en, reset
  and and_12 (and_12_out, ~b2, ~b1, b3);  // AND_Gate
  and and_13 (and_13_out, b0, ~b1);  // AND_Gate
  and and_14 (and_14_out, ~b0, b2, b1);  // AND_Gate
  and and_15 (and_15_out, b1, ~b3);  // AND_Gate
  or or_4 (d0, and_12_out, and_13_out, and_14_out, and_15_out);
endmodule

module jk (
  output [3:0] out_1
);

  wire j0, j2, k1, k2, reloj, reset;

  Clock clock_1 (.out(reloj));
  Button button_1 (.out(reset));
  not not_1 (j0, out_1[1]);
  J_K_Flip_Flop j_k_ff_1 (
    .J(out_1[0]), .clk(reloj), .K(out_1[2]), .Q(out_1[3]), .preset(reset));  // open: Qn, en, reset
  and and_1 (k1, ~out_1[3], out_1[2]);  // AND_Gate
  J_K_Flip_Flop j_k_ff_2 (.J(j2), .clk(reloj), .K(k2), .Q(out_1[2]), .preset(reset));  // open: Qn, en, reset
  J_K_Flip_Flop j_k_ff_3 (.J(1'b1), .clk(reloj), .K(k1), .Q(out_1[1]), .preset(reset));  // open: Qn, en, reset
  or or_1 (j2, out_1[3], ~out_1[0]);  // OR_Gate
  or or_2 (k2, out_1[3], ~out_1[1]);  // OR_Gate
  J_K_Flip_Flop j_k_ff_4 (.J(j0), .clk(reloj), .K(out_1[3]), .Q(out_1[0]), .preset(reset));  // open: Qn, en, reset

  // Other names for the same wires on the sheet: b3 = out_1[0]; j3 = out_1[0]; b2 = out_1[1]; b1 = out_1[2];
  //   k3 = out_1[2]; b0 = out_1[3]; k0 = out_1[3]
endmodule
